// Logisim project CE1r1.circ as structural Verilog: 1 circuit, main circuit main
module main (
  input  In1,
  input  In2,
  input  In3,
  output Out1,
  output Out2
);

  wire and_1_out, and_2_out, and_3_out, and_4_out, and_5_out, not_1_out, not_2_out, not_3_out, not_4_out,
       not_5_out, or_1_out, xor_1_out;

  xor xor_1 (xor_1_out, In2, In1);
  not not_1 (not_1_out, In3);
  not not_2 (not_2_out, In2);
  not not_3 (not_3_out, In1);
  xor xor_2 (In1, In2, In3);
  or or_1 (or_1_out, not_1_out, In3);
  and and_1 (and_1_out, not_2_out, not_3_out);
  not not_4 (not_4_out, In1);
  not not_5 (not_5_out, In1);
  and and_2 (and_2_out, xor_1_out, not_1_out);
  and and_3 (and_3_out, or_1_out, and_1_out);
  and and_4 (and_4_out, not_4_out, not_5_out);
  or or_2 (Out1, and_2_out, and_3_out);
  and and_5 (and_5_out, not_5_out, In1);
  or or_3 (Out2, and_4_out, and_5_out);
endmodule
