// Logisim project CE2.circ as structural Verilog: 1 circuit, main circuit main
module main (
  input  A1,
  input  A2,
  input  A3,
  input  A4,
  input  W,
  input  S,
  output out_7,
  output out_8,
  output out_9,
  output out_10
);

  wire and_1_out, and_2_out, and_3_out, and_4_out, and_5_out, and_6_out, and_7_out, and_8_out, and_9_out,
       buffer_1_out, buffer_2_out, ClockR_out, or_1_out, or_2_out, or_3_out, or_4_out, or_5_out, Reset_out;

  Button Reset (.out(Reset_out));
  and and_1 (and_1_out, A1, W);
  and and_2 (and_2_out, A2, W);
  and and_3 (and_3_out, A3, W);
  and and_4 (and_4_out, A4, W);
  buf buffer_1 (buffer_1_out, W);
  buf buffer_2 (buffer_2_out, S);
  and and_5 (and_5_out, out_10, S);
  and and_6 (and_6_out, out_7, S);
  and and_7 (and_7_out, out_8, S);
  and and_8 (and_8_out, out_9, S);
  Clock #(.phaseOffset(1)) ClockR (.out(ClockR_out));
  or or_1 (or_1_out, buffer_1_out, buffer_2_out);
  or or_2 (or_2_out, and_1_out, and_5_out);
  or or_3 (or_3_out, and_2_out, and_6_out);
  or or_4 (or_4_out, and_3_out, and_7_out);
  or or_5 (or_5_out, and_4_out, and_8_out);
  and and_9 (and_9_out, ClockR_out, or_1_out);
  D_Flip_Flop d_ff_1 (.D(or_2_out), .clk(and_9_out), .Q(out_7), .reset(Reset_out));  // open: Qn, preset
  D_Flip_Flop d_ff_2 (.D(or_3_out), .clk(and_9_out), .Q(out_8), .reset(Reset_out));  // open: Qn, preset
  D_Flip_Flop d_ff_3 (.D(or_4_out), .clk(and_9_out), .Q(out_9), .reset(Reset_out));  // open: Qn, preset
  D_Flip_Flop d_ff_4 (.D(or_5_out), .clk(and_9_out), .Q(out_10), .reset(Reset_out));  // open: Qn, preset
endmodule
