// Logisim project EsoneroC.circ as structural Verilog: 1 circuit, main circuit main
module main (
  input  in_1,
  input  in_2,
  input  in_3,
  input  in_4,
  input  W,
  output out_6,
  output out_7,
  output out_8,
  output out_9,
  output out_10,
  output out_11,
  output out_12,
  output out_13
);

  wire adder_2_cout, adder_3_cout, adder_4_cout, and_1_out, clock_1_out, not_1_out, not_2_out, not_3_out,
       not_4_out, not_5_out;

  not not_1 (not_1_out, W);
  Clock clock_1 (.out(clock_1_out));
  and and_1 (and_1_out, clock_1_out, W);
  D_Flip_Flop d_ff_1 (.D(in_1), .clk(and_1_out), .Q(out_6));  // open: Qn, preset, reset
  D_Flip_Flop d_ff_2 (.D(in_2), .clk(and_1_out), .Q(out_7));  // open: Qn, preset, reset
  D_Flip_Flop d_ff_3 (.D(in_3), .clk(and_1_out), .Q(out_8));  // open: Qn, preset, reset
  D_Flip_Flop d_ff_4 (.D(in_4), .clk(and_1_out), .Q(out_9));  // open: Qn, preset, reset
  // AND_Gate and_2 has open pins: in1=not_1_out, out=open
  // AND_Gate and_3 has open pins: in1=not_1_out, out=open
  // AND_Gate and_4 has open pins: in0=out_8, in1=not_1_out, out=open
  // AND_Gate and_5 has open pins: in0=out_9, in1=not_1_out, out=open
  not not_2 (not_2_out, out_6);
  not not_3 (not_3_out, out_7);
  not not_4 (not_4_out, out_8);
  not not_5 (not_5_out, out_9);
  Adder #(.width(1)) adder_1 (.a(not_2_out), .b(adder_2_cout), .out(out_10));  // open: cin, cout
  Adder #(.width(1)) adder_2 (.a(not_3_out), .b(adder_3_cout), .out(out_11), .cout(adder_2_cout));  // open: cin
  Adder #(.width(1)) adder_3 (.a(not_4_out), .b(adder_4_cout), .out(out_12), .cout(adder_3_cout));  // open: cin
  Adder #(.width(1)) adder_4 (.a(1'b1), .b(not_5_out), .out(out_13), .cout(adder_4_cout));  // open: cin
endmodule
